// Logisim project fsm.circ as structural Verilog: 3 circuits, main circuit fsm
module fsm (
  input  in_1,
  input  [1:0] in_2,
  output out_3
);

  wire clock_1_out;
  wire [1:0] multiplexer_1_out, register_1_q, status_1_s0_2;

  Clock clock_1 (.out(clock_1_out));
  status status_1 (
    .s1(register_1_q[1]), .s0(register_1_q[0]), .a(in_2[1]), .b(in_2[0]), .s1_2(status_1_s0_2[1]),
    .s0_2(status_1_s0_2[0]));
  Multiplexer #(.width(2)) multiplexer_1 (
    .in0(status_1_s0_2), .in1(2'b00), .out(multiplexer_1_out), .sel(in_1));  // open: en
  Register #(.width(2)) register_1 (.D(multiplexer_1_out), .Q(register_1_q), .clk(clock_1_out));  // open: en, clr
  \output  output_1 (.s1(register_1_q[1]), .s0(register_1_q[0]), .a(in_2[1]), .b(in_2[0]), .r(out_3));

  // Other names for the same wires on the sheet: clear = in_1
endmodule

module status (
  input  s1,
  input  s0,
  input  a,
  input  b,
  output s1_2,
  output s0_2
);

  wire and_1_out, and_2_out, and_3_out, and_4_out, not_1_out, not_2_out, not_3_out, not_4_out, not_5_out,
       not_6_out, not_7_out;

  not not_1 (not_1_out, s1);
  and and_1 (and_1_out, not_1_out, s0, not_2_out);
  not not_2 (not_2_out, b);
  and and_2 (and_2_out, s1, not_3_out, not_4_out);
  not not_3 (not_3_out, s0);
  not not_4 (not_4_out, b);
  not not_5 (not_5_out, a);
  and and_3 (and_3_out, not_5_out, b);
  not not_6 (not_6_out, s0);
  and and_4 (and_4_out, s1, not_6_out, not_7_out);
  not not_7 (not_7_out, b);
  or or_1 (s1_2, and_1_out, and_2_out);
  or or_2 (s0_2, and_3_out, and_4_out);
endmodule

module \output  (
  input  s1,
  input  s0,
  input  a,
  input  b,
  output r
);

  wire not_1_out, not_2_out;

  not not_1 (not_1_out, s0);
  and and_1 (r, s1, not_1_out, not_2_out);
  not not_2 (not_2_out, b);
endmodule
