// Logisim project ftoi.circ as structural Verilog: 1 circuit, main circuit ftoi
module ftoi (
  input  [15:0] in_1,
  output [31:0] out_2
);

  wire comparator_1_eq, comparator_2_eq, comparator_3_lt, comparator_4_gt, or_1_out;
  wire [4:0] subtractor_1_out, subtractor_2_out, subtractor_3_out;
  wire [30:0] multiplexer_1_out, multiplexer_3_out, negator_1_out, shifter_1_out, shifter_2_out;

  Subtractor #(.width(5)) subtractor_1 (.a(in_1[14:10]), .b(5'b01111), .out(subtractor_1_out));  // open: bin, bout
  Comparator #(.width(5)) comparator_1 (.a(in_1[14:10]), .b({5{1'b1}}), .eq(comparator_1_eq));  // open: gt, lt
  Comparator #(.width(5)) comparator_2 (.a(in_1[14:10]), .b({5{1'b0}}), .eq(comparator_2_eq));  // open: gt, lt
  Comparator #(.width(5)) comparator_3 (.a(subtractor_1_out), .b({5{1'b0}}), .lt(comparator_3_lt));  // open: gt, eq
  Comparator #(.width(5)) comparator_4 (.a(subtractor_1_out), .b(5'b01001), .gt(comparator_4_gt));  // open: eq, lt
  Subtractor #(.width(5)) subtractor_2 (.a(subtractor_1_out), .b(5'b01010), .out(subtractor_2_out));  // open: bin, bout
  Subtractor #(.width(5)) subtractor_3 (.a(5'b01010), .b(subtractor_1_out), .out(subtractor_3_out));  // open: bin, bout
  or or_1 (or_1_out, comparator_1_eq, comparator_2_eq, comparator_3_lt);
  Shifter #(.width(31)) shifter_1 (.in({21'h1, in_1[9:0]}), .\dist (subtractor_2_out), .out(shifter_1_out));
  Shifter #(.width(31), .shift("lr")) shifter_2 (
    .in({21'h1, in_1[9:0]}), .\dist (subtractor_3_out), .out(shifter_2_out));
  Multiplexer #(.width(31)) multiplexer_1 (
    .in0(shifter_2_out), .in1(shifter_1_out), .out(multiplexer_1_out), .sel(comparator_4_gt));  // open: en
  Multiplexer #(.width(32)) multiplexer_2 (
    .in0({in_1[15], multiplexer_3_out}), .in1({32{1'b0}}), .out(out_2), .sel(or_1_out));  // open: en
  Negator #(.width(31)) negator_1 (.in(multiplexer_1_out), .out(negator_1_out));
  Multiplexer #(.width(31)) multiplexer_3 (
    .in0(multiplexer_1_out), .in1(negator_1_out), .out(multiplexer_3_out), .sel(in_1[15]));  // open: en
endmodule
