// Logisim project navigation.circ as structural Verilog: 2 circuits, main circuit navigation
module navigation (
  input  [1:0] in_1,
  input  in_2,
  input  in_3,
  output arrive,
  output hit
);

  wire status_2_arrive, status_2_hit;
  wire [2:0] register_1_q, status_1_s02;

  status status_1 (
    .s2(register_1_q[2]), .s1(register_1_q[1]), .s0(register_1_q[0]), .a(in_1[1]), .b(in_1[0]),
    .s22(status_1_s02[2]), .s12(status_1_s02[1]), .s02(status_1_s02[0]));  // open: hit, arrive
  Register #(.width(3)) register_1 (.D(status_1_s02), .Q(register_1_q), .clk(in_2), .clr(in_3));  // open: en
  status status_2 (
    .s2(register_1_q[2]), .s1(register_1_q[1]), .s0(register_1_q[0]), .a(in_1[1]), .b(in_1[0]),
    .hit(status_2_hit), .arrive(status_2_arrive));  // open: s22, s12, s02
  Register #(.width(1)) register_2 (.D(status_2_hit), .Q(hit), .clk(in_2), .clr(in_3));  // open: en
  Register #(.width(1)) register_3 (.D(status_2_arrive), .Q(arrive), .clk(in_2), .clr(in_3));  // open: en

  // Other names for the same wires on the sheet: clk = in_2; reset = in_3
endmodule

module status (
  input  s2,
  input  s1,
  input  s0,
  input  a,
  input  b,
  output s22,
  output s12,
  output s02,
  output hit,
  output arrive
);

  wire and_1_out, and_2_out, and_3_out, and_4_out, and_5_out, and_6_out, and_7_out, and_8_out, and_9_out,
       and_10_out, and_11_out, and_12_out, and_13_out, and_14_out, and_15_out, and_16_out, and_17_out,
       and_18_out, and_19_out, not_1_out, not_2_out, not_3_out, not_4_out, not_5_out, not_6_out, not_7_out,
       not_8_out, not_9_out, not_10_out, not_11_out, not_12_out, not_13_out, not_14_out, not_15_out,
       not_16_out, not_17_out, not_18_out, not_19_out, not_20_out, not_21_out, not_22_out, not_23_out,
       not_24_out, not_25_out, not_26_out, not_27_out, not_28_out, not_29_out, not_30_out, not_31_out,
       not_32_out, not_33_out, not_34_out, not_35_out, not_36_out, not_37_out, not_38_out, not_39_out,
       not_40_out, not_41_out, not_42_out, not_43_out, not_44_out, not_45_out, not_46_out, not_47_out,
       not_48_out, not_49_out, not_50_out, not_51_out;

  not not_1 (not_1_out, s2);
  not not_2 (not_2_out, s0);
  not not_3 (not_3_out, a);
  not not_4 (not_4_out, s2);
  not not_5 (not_5_out, a);
  not not_6 (not_6_out, b);
  not not_7 (not_7_out, s2);
  not not_8 (not_8_out, s1);
  not not_9 (not_9_out, a);
  not not_10 (not_10_out, s2);
  not not_11 (not_11_out, a);
  not not_12 (not_12_out, s2);
  not not_13 (not_13_out, s0);
  not not_14 (not_14_out, a);
  not not_15 (not_15_out, b);
  not not_16 (not_16_out, s2);
  not not_17 (not_17_out, s0);
  not not_18 (not_18_out, s2);
  not not_19 (not_19_out, b);
  not not_20 (not_20_out, s2);
  not not_21 (not_21_out, s1);
  not not_22 (not_22_out, s0);
  not not_23 (not_23_out, a);
  not not_24 (not_24_out, b);
  not not_25 (not_25_out, s2);
  not not_26 (not_26_out, s2);
  not not_27 (not_27_out, b);
  not not_28 (not_28_out, s2);
  not not_29 (not_29_out, s1);
  not not_30 (not_30_out, s0);
  not not_31 (not_31_out, s2);
  not not_32 (not_32_out, s1);
  not not_33 (not_33_out, s0);
  not not_34 (not_34_out, s2);
  not not_35 (not_35_out, s1);
  not not_36 (not_36_out, s2);
  not not_37 (not_37_out, s0);
  not not_38 (not_38_out, s2);
  not not_39 (not_39_out, s0);
  not not_40 (not_40_out, a);
  not not_41 (not_41_out, b);
  not not_42 (not_42_out, s2);
  not not_43 (not_43_out, a);
  not not_44 (not_44_out, s2);
  not not_45 (not_45_out, b);
  not not_46 (not_46_out, s2);
  not not_47 (not_47_out, s0);
  not not_48 (not_48_out, a);
  not not_49 (not_49_out, s2);
  not not_50 (not_50_out, a);
  not not_51 (not_51_out, b);
  and and_1 (and_1_out, not_1_out, s1, not_2_out, not_3_out, b);
  and and_2 (and_2_out, not_4_out, s1, s0, not_5_out, not_6_out);
  and and_3 (and_3_out, not_7_out, not_8_out, s0, not_9_out);
  and and_4 (and_4_out, not_10_out, s0, not_11_out, b);
  and and_5 (and_5_out, not_12_out, s1, not_13_out, not_14_out, not_15_out);
  and and_6 (and_6_out, not_16_out, s1, not_17_out, a, b);
  and and_7 (and_7_out, not_18_out, s1, s0, a, not_19_out);
  and and_8 (and_8_out, not_20_out, not_21_out, not_22_out, not_23_out, not_24_out);
  and and_9 (and_9_out, not_25_out, s0, b);
  and and_10 (and_10_out, not_26_out, s1, a, not_27_out);
  and and_11 (and_11_out, not_28_out, not_29_out, not_30_out, b);
  and and_12 (and_12_out, not_31_out, not_32_out, not_33_out, a);
  and and_13 (and_13_out, not_34_out, not_35_out, a, b);
  and and_14 (and_14_out, not_36_out, not_37_out, a, b);
  and and_15 (and_15_out, not_38_out, s1, not_39_out, not_40_out, not_41_out);
  and and_16 (and_16_out, not_42_out, s1, s0, not_43_out, b);
  and and_17 (and_17_out, not_44_out, s1, s0, a, not_45_out);
  and and_18 (and_18_out, not_46_out, s1, not_47_out, not_48_out, b);
  and and_19 (and_19_out, not_49_out, s1, s0, not_50_out, not_51_out);
  or or_1 (s22, and_1_out, and_2_out);
  or or_2 (s12, and_3_out, and_4_out, and_5_out, and_6_out, and_7_out);
  or or_3 (s02, and_8_out, and_9_out, and_10_out);
  or or_4 (hit, and_11_out, and_12_out, and_13_out, and_14_out, and_15_out, and_16_out, and_17_out);
  or or_5 (arrive, and_18_out, and_19_out);
endmodule
