// Logisim project main.circ as structural Verilog: 9 circuits, main circuit main
module main (
  input  in_1,
  output [31:0] out_2,
  output out_3,
  output [4:0] out_4,
  output [31:0] out_5,
  output out_6,
  output [4:0] out_7,
  output [31:0] out_8
);

  wire AluSrc, and_2_out, Branch, clk, controller_1_out_14, controller_1_out_15, controller_1_out_17,
       controller_1_out_18, controller_1_regwrite, J, JAL, JR, MemRead, MemtoReg, nop, RegDst;
  wire [1:0] Sign;
  wire [3:0] AluControl;
  wire [4:0] multiplexer_1_out, opsplitter_1_rd, opsplitter_1_rs, opsplitter_1_rt, opsplitter_1_shamt,
       pc_1_out_4;
  wire [5:0] opsplitter_1_func, opsplitter_1_op;
  wire [15:0] opsplitter_1_imme;
  wire [25:0] opsplitter_1_address;
  wire [31:0] adder_1_out, alu_1_out_5, dm_1_out_12, ext_1_out_3, grf_1_rdrs, multiplexer_3_out,
       multiplexer_4_out, npc_1_out_8, pc_1_pc;

  Clock clock_1 (.out(clk));
  NPC npc_1 (
    .in_1(pc_1_pc), .out_8(npc_1_out_8), .in_3(and_2_out), .in_2(ext_1_out_3), .in_5(J),
    .in_4(opsplitter_1_address), .in_6(grf_1_rdrs), .in_7(JR));
  PC pc_1 (.in_1(npc_1_out_8), .clk(clk), .reset(in_1), .PC(pc_1_pc), .out_4(pc_1_out_4));
  Comparator #(.width(32), .mode("unsigned")) comparator_1 (.a(out_2), .b({32{1'b0}}), .gt(nop));  // open: eq, lt
  ROM #(.addrWidth(5), .dataWidth(32)) rom_1 (.addr(pc_1_out_4), .data(out_2));  // open: sel
  OPSPLITTER opsplitter_1 (
    .in_1(out_2), .OP(opsplitter_1_op), .RS(opsplitter_1_rs), .RT(opsplitter_1_rt), .RD(opsplitter_1_rd),
    .SHAMT(opsplitter_1_shamt), .FUNC(opsplitter_1_func), .IMME(opsplitter_1_imme),
    .ADDRESS(opsplitter_1_address));
  Adder #(.width(32)) adder_1 (.a(pc_1_pc), .b(32'h4), .out(adder_1_out));  // open: cin, cout
  Multiplexer #(.width(5)) multiplexer_1 (
    .in0(opsplitter_1_rt), .in1(opsplitter_1_rd), .out(multiplexer_1_out), .sel(RegDst));  // open: en
  EXT ext_1 (.in_1(opsplitter_1_imme), .out_3(ext_1_out_3), .in_2(Sign));
  Controller controller_1 (
    .FUNC(opsplitter_1_func), .OP(opsplitter_1_op), .out_16(AluControl), .RegDst(RegDst), .AluSrc(AluSrc),
    .MemtoReg(MemtoReg), .Branch(Branch), .RegWrite(controller_1_regwrite), .MemWrite(out_6),
    .MemRead(MemRead), .Sign(Sign), .J(J), .out_12(JAL), .out_13(JR), .out_15(controller_1_out_15),
    .out_17(controller_1_out_17), .out_18(controller_1_out_18), .out_14(controller_1_out_14));
  Multiplexer #(.width(5)) multiplexer_2 (
    .in0(multiplexer_1_out), .in1({5{1'b1}}), .out(out_4), .sel(JAL));  // open: en
  and and_1 (out_3, controller_1_regwrite, nop);
  GRF grf_1 (
    .RDRS(grf_1_rdrs), .RDRT(out_8), .clk(clk), .clr(in_1), .RegWrite(out_3), .Rs(opsplitter_1_rs),
    .Rt(opsplitter_1_rt), .Rd(out_4), .WriteData(out_5));
  Multiplexer #(.width(32)) multiplexer_3 (
    .in0(out_8), .in1(ext_1_out_3), .out(multiplexer_3_out), .sel(AluSrc));  // open: en
  ALU alu_1 (
    .in_1(grf_1_rdrs), .in_2(multiplexer_3_out), .op(AluControl), .out_5(alu_1_out_5),
    .SHAMT(opsplitter_1_shamt));
  and and_2 (and_2_out, Branch, alu_1_out_5[0]);
  DM dm_1 (
    .in_1(alu_1_out_5), .clk(clk), .MemRead(MemRead), .clr(in_1), .in_3(out_8), .MemWrite(out_6),
    .out_11(out_7), .out_12(dm_1_out_12), .LB(controller_1_out_15), .LH(controller_1_out_17),
    .SB(controller_1_out_18), .SH(controller_1_out_14));
  Multiplexer #(.width(32)) multiplexer_4 (
    .in0(alu_1_out_5), .in1(dm_1_out_12), .out(multiplexer_4_out), .sel(MemtoReg));  // open: en
  Multiplexer #(.width(32)) multiplexer_5 (
    .in0(multiplexer_4_out), .in1(adder_1_out), .out(out_5), .sel(JAL));  // open: en

  // Other names for the same wires on the sheet: clr = in_1; Instr[31:0] = out_2; MemAddr[4:0] = out_7;
  //   MemData[31:0] = out_8; MemWrite = out_6; RegAddr[4:0] = out_4; RegData[31:0] = out_5; RegWrite = out_3
endmodule

module GRF (
  input  clk,
  input  clr,
  input  RegWrite,
  input  [4:0] Rs,
  input  [4:0] Rt,
  input  [4:0] Rd,
  input  [31:0] WriteData,
  output [31:0] RDRS,
  output [31:0] RDRT
);

  wire [31:0] _0D, _1D, _1Q, _2D, _2Q, _3D, _3Q, _4D, _4Q, _5D, _5Q, _6D, _6Q, _7D, _7Q, _8D, _8Q, _9D, _9Q,
       _10D, _10Q, _11D, _11Q, _12D, _12Q, _13D, _13Q, _14D, _14Q, _15D, _15Q, _16D, _16Q, _17D, _17Q, _18D,
       _18Q, _19D, _19Q, _20D, _20Q, _21D, _21Q, _22D, _22Q, _23D, _23Q, _24D, _24Q, _25D, _25Q, _26D, _26Q,
       _27D, _27Q, _28D, _28Q, _29D, _29Q, _30D, _30Q, _31D, _31Q;

  Register #(.width(32)) register_1 (.D(_8D), .en(RegWrite), .Q(_8Q), .clk(clk), .clr(clr));
  Register #(.width(32)) register_2 (.D(_16D), .en(RegWrite), .Q(_16Q), .clk(clk), .clr(clr));
  Register #(.width(32)) register_3 (.D(_24D), .en(RegWrite), .Q(_24Q), .clk(clk), .clr(clr));
  Register #(.width(32)) register_4 (.D(_1D), .en(RegWrite), .Q(_1Q), .clk(clk), .clr(clr));
  Register #(.width(32)) register_5 (.D(_9D), .en(RegWrite), .Q(_9Q), .clk(clk), .clr(clr));
  Register #(.width(32)) register_6 (.D(_17D), .en(RegWrite), .Q(_17Q), .clk(clk), .clr(clr));
  Register #(.width(32)) register_7 (.D(_25D), .en(RegWrite), .Q(_25Q), .clk(clk), .clr(clr));
  Demultiplexer #(.select(5), .width(32), .tristate("true")) demultiplexer_1 (
    .out0(_0D), .out1(_1D), .out2(_2D), .out3(_3D), .out4(_4D), .out5(_5D), .out6(_6D), .out7(_7D),
    .out8(_8D), .out9(_9D), .out10(_10D), .out11(_11D), .out12(_12D), .out13(_13D), .out14(_14D),
    .out15(_15D), .out16(_16D), .out17(_17D), .out18(_18D), .out19(_19D), .out20(_20D), .out21(_21D),
    .out22(_22D), .out23(_23D), .out24(_24D), .out25(_25D), .out26(_26D), .out27(_27D), .out28(_28D),
    .out29(_29D), .out30(_30D), .out31(_31D), .in(WriteData), .sel(Rd));  // open: en
  Register #(.width(32)) register_8 (.D(_2D), .en(RegWrite), .Q(_2Q), .clk(clk), .clr(clr));
  Register #(.width(32)) register_9 (.D(_10D), .en(RegWrite), .Q(_10Q), .clk(clk), .clr(clr));
  Register #(.width(32)) register_10 (.D(_18D), .en(RegWrite), .Q(_18Q), .clk(clk), .clr(clr));
  Register #(.width(32)) register_11 (.D(_26D), .en(RegWrite), .Q(_26Q), .clk(clk), .clr(clr));
  Register #(.width(32)) register_12 (.D(_3D), .en(RegWrite), .Q(_3Q), .clk(clk), .clr(clr));
  Register #(.width(32)) register_13 (.D(_11D), .en(RegWrite), .Q(_11Q), .clk(clk), .clr(clr));
  Register #(.width(32)) register_14 (.D(_19D), .en(RegWrite), .Q(_19Q), .clk(clk), .clr(clr));
  Register #(.width(32)) register_15 (.D(_27D), .en(RegWrite), .Q(_27Q), .clk(clk), .clr(clr));
  Register #(.width(32)) register_16 (.D(_4D), .en(RegWrite), .Q(_4Q), .clk(clk), .clr(clr));
  Register #(.width(32)) register_17 (.D(_12D), .en(RegWrite), .Q(_12Q), .clk(clk), .clr(clr));
  Register #(.width(32)) register_18 (.D(_20D), .en(RegWrite), .Q(_20Q), .clk(clk), .clr(clr));
  Register #(.width(32)) register_19 (.D(_28D), .en(RegWrite), .Q(_28Q), .clk(clk), .clr(clr));
  Register #(.width(32)) register_20 (.D(_5D), .en(RegWrite), .Q(_5Q), .clk(clk), .clr(clr));
  Register #(.width(32)) register_21 (.D(_6D), .en(RegWrite), .Q(_6Q), .clk(clk), .clr(clr));
  Register #(.width(32)) register_22 (.D(_13D), .en(RegWrite), .Q(_13Q), .clk(clk), .clr(clr));
  Register #(.width(32)) register_23 (.D(_21D), .en(RegWrite), .Q(_21Q), .clk(clk), .clr(clr));
  Register #(.width(32)) register_24 (.D(_29D), .en(RegWrite), .Q(_29Q), .clk(clk), .clr(clr));
  Multiplexer #(.select(5), .width(32)) multiplexer_1 (
    .in0({32{1'b0}}), .in1(_1Q), .in2(_2Q), .in3(_3Q), .in4(_4Q), .in5(_5Q), .in6(_6Q), .in7(_7Q), .in8(_8Q),
    .in9(_9Q), .in10(_10Q), .in11(_11Q), .in12(_12Q), .in13(_13Q), .in14(_14Q), .in15(_15Q), .in16(_16Q),
    .in17(_17Q), .in18(_18Q), .in19(_19Q), .in20(_20Q), .in21(_21Q), .in22(_22Q), .in23(_23Q), .in24(_24Q),
    .in25(_25Q), .in26(_26Q), .in27(_27Q), .in28(_28Q), .in29(_29Q), .in30(_30Q), .in31(_31Q), .out(RDRS),
    .sel(Rs));  // open: en
  Register #(.width(32)) register_25 (.D(_7D), .en(RegWrite), .Q(_7Q), .clk(clk), .clr(clr));
  Register #(.width(32)) register_26 (.D(_14D), .en(RegWrite), .Q(_14Q), .clk(clk), .clr(clr));
  Register #(.width(32)) register_27 (.D(_22D), .en(RegWrite), .Q(_22Q), .clk(clk), .clr(clr));
  Register #(.width(32)) register_28 (.D(_30D), .en(RegWrite), .Q(_30Q), .clk(clk), .clr(clr));
  Register #(.width(32)) register_29 (.D(_15D), .en(RegWrite), .Q(_15Q), .clk(clk), .clr(clr));
  Register #(.width(32)) register_30 (.D(_23D), .en(RegWrite), .Q(_23Q), .clk(clk), .clr(clr));
  Register #(.width(32)) register_31 (.D(_31D), .en(RegWrite), .Q(_31Q), .clk(clk));  // open: clr
  Multiplexer #(.select(5), .width(32)) multiplexer_2 (
    .in0({32{1'b0}}), .in1(_1Q), .in2(_2Q), .in3(_3Q), .in4(_4Q), .in5(_5Q), .in6(_6Q), .in7(_7Q), .in8(_8Q),
    .in9(_9Q), .in10(_10Q), .in11(_11Q), .in12(_12Q), .in13(_13Q), .in14(_14Q), .in15(_15Q), .in16(_16Q),
    .in17(_17Q), .in18(_18Q), .in19(_19Q), .in20(_20Q), .in21(_21Q), .in22(_22Q), .in23(_23Q), .in24(_24Q),
    .in25(_25Q), .in26(_26Q), .in27(_27Q), .in28(_28Q), .in29(_29Q), .in30(_30Q), .in31(_31Q), .out(RDRT),
    .sel(Rt));  // open: en

  // Other names for the same wires on the sheet: A1[4:0] = Rs; A2[4:0] = Rt; A3[4:0] = Rd; RD1[31:0] = RDRS;
  //   RD2[31:0] = RDRT; reset = clr; WD[31:0] = WriteData; we = RegWrite
endmodule

module PC (
  input  [31:0] in_1,
  input  clk,
  input  reset,
  output [4:0] out_4,
  output [31:0] PC
);

  Register #(.width(32)) register_1 (.D(in_1), .Q({PC[31:7], out_4, PC[1:0]}), .clk(clk), .clr(reset));  // open: en

  assign PC[6:2] = out_4;
endmodule

module ALU (
  input  [31:0] in_1,
  input  [31:0] in_2,
  input  [4:0] SHAMT,
  input  [3:0] op,
  output [31:0] out_5
);

  wire comparator_1_eq;
  wire [31:0] adder_1_out, bit_extender_1_out, or_1_out, shifter_1_out, shifter_2_out, subtractor_1_out;

  Adder #(.width(32)) adder_1 (.a(in_1), .b(in_2), .out(adder_1_out));  // open: cin, cout
  Shifter #(.width(32)) shifter_1 (.in(in_2), .\dist (SHAMT), .out(shifter_1_out));
  Shifter #(.width(32), .shift("lr")) shifter_2 (.in(in_2), .\dist (SHAMT), .out(shifter_2_out));
  Subtractor #(.width(32)) subtractor_1 (.a(in_1), .b(in_2), .out(subtractor_1_out));  // open: bin, bout
  assign or_1_out = in_1 | in_2;  // OR_Gate or_1, 32 bits wide
  Comparator #(.width(32)) comparator_1 (.a(in_1), .b(in_2), .eq(comparator_1_eq));  // open: gt, lt
  assign bit_extender_1_out = {{31{1'b0}}, comparator_1_eq};  // Bit_Extender bit_extender_1
  Multiplexer #(.select(4), .width(32)) multiplexer_1 (
    .in0(adder_1_out), .in1(subtractor_1_out), .in2(or_1_out), .in3(bit_extender_1_out), .in4(shifter_1_out),
    .in5(shifter_2_out), .out(out_5), .sel(op));  // open: in6, in7, in8, in9, in10, in11, in12, in13, in14, in15, en
endmodule

module Controller (
  input  [5:0] FUNC,
  input  [5:0] OP,
  output [1:0] Sign,
  output RegDst,
  output AluSrc,
  output Branch,
  output MemWrite,
  output MemtoReg,
  output RegWrite,
  output MemRead,
  output J,
  output out_12,
  output out_13,
  output out_14,
  output out_15,
  output [3:0] out_16,
  output out_17,
  output out_18
);

  wire ADD, BEQ, J_t, JAL, JR, LB, LH, LUI, LW, not_1_out, not_2_out, not_3_out, not_4_out, not_5_out,
       not_6_out, not_7_out, not_8_out, not_9_out, not_10_out, not_11_out, not_12_out, or_6_out, or_9_out,
       ORI, RTYPE_out, SB, SH, SLL, SRL, SUB, SW;

  not not_1 (not_1_out, OP[5]);
  or or_1 (RegDst, 1'b0, ADD, SUB, SLL, SRL);
  not not_2 (not_2_out, OP[4]);
  not not_3 (not_3_out, OP[3]);
  not not_4 (not_4_out, OP[2]);
  not not_5 (not_5_out, OP[0]);
  not not_6 (not_6_out, OP[1]);
  and RTYPE (RTYPE_out, not_1_out, not_2_out, not_3_out, not_4_out, not_6_out, not_5_out);
  and u_BEQ (BEQ, not_1_out, not_2_out, not_3_out, OP[2], not_6_out, not_5_out);
  and u_LW (LW, OP[5], not_2_out, not_3_out, not_4_out, OP[1], OP[0]);
  and u_SW (SW, OP[5], not_2_out, OP[3], not_4_out, OP[1], OP[0]);
  and u_ORI (ORI, not_1_out, not_2_out, OP[3], OP[2], not_6_out, OP[0]);
  and u_LUI (LUI, not_1_out, not_2_out, OP[3], OP[2], OP[1], OP[0]);
  and u_J (J_t, not_1_out, not_2_out, not_3_out, not_4_out, OP[1], not_5_out);
  and u_JAL (JAL, not_1_out, not_2_out, not_3_out, not_4_out, OP[1], OP[0]);
  and u_LB (LB, OP[5], not_2_out, not_3_out, not_4_out, not_6_out, not_5_out);
  and u_LH (LH, OP[5], not_2_out, not_3_out, not_4_out, not_6_out, OP[0]);
  and u_SB (SB, OP[5], not_2_out, OP[3], not_4_out, not_6_out, not_5_out);
  and u_SH (SH, OP[5], not_2_out, OP[3], not_4_out, not_6_out, OP[0]);
  or or_2 (AluSrc, 1'b0, LW, SW, ORI, LUI, LB, LH, SB, SH);
  or or_3 (MemtoReg, 1'b0, LW, LB, LH);
  not not_7 (not_7_out, FUNC[5]);
  not not_8 (not_8_out, FUNC[4]);
  not not_9 (not_9_out, FUNC[3]);
  not not_10 (not_10_out, FUNC[2]);
  or or_4 (Branch, 1'b0, BEQ);
  not not_11 (not_11_out, FUNC[1]);
  not not_12 (not_12_out, FUNC[0]);
  or or_5 (RegWrite, 1'b0, LB, LH, ADD, LW, ORI, LUI, SUB, JAL, SLL, SRL);
  and u_ADD (ADD, FUNC[5], not_8_out, not_9_out, not_10_out, not_11_out, not_12_out, RTYPE_out);
  and u_SUB (SUB, FUNC[5], not_8_out, not_9_out, not_10_out, FUNC[1], not_12_out, RTYPE_out);
  or or_6 (or_6_out, LUI, SW, LW, ADD);
  or or_7 (MemRead, 1'b0, LW, LB, LH, SB, SH);
  or or_8 (MemWrite, 1'b0, SW, SB, SH);
  Priority_Encoder #(.select(4)) priority_encoder_1 (
    .in0(or_6_out), .in1(SUB), .in2(ORI), .in3(BEQ), .in4(SLL), .in5(SRL), .out(out_16));  // open: in6, in7, in8, in9, in10, in11, in12, in13, in14, in15, gs, en_out, en_in
  Pull_Resistor pull_resistor_1 (.node(out_16));
  or or_9 (or_9_out, SH, SB, SW, LH, BEQ, LB, LW);
  Pull_Resistor pull_resistor_2 (.node(Sign));
  Priority_Encoder #(.select(2)) priority_encoder_2 (
    .in0(ORI), .in1(or_9_out), .in2(LUI), .out(Sign));  // open: in3, gs, en_out, en_in
  or or_10 (J, 1'b0, J_t, JAL);
  or or_11 (out_12, 1'b0, JAL);
  or or_12 (out_13, 1'b0, JR);
  or or_13 (out_15, 1'b0, LB);
  or or_14 (out_17, 1'b0, LH);
  and u_JR (JR, not_7_out, not_8_out, FUNC[3], RTYPE_out, not_10_out, not_11_out, not_12_out);
  and u_SLL (SLL, not_7_out, not_8_out, not_9_out, RTYPE_out, not_10_out, not_11_out, not_12_out);
  and u_SRL (SRL, not_7_out, not_8_out, not_9_out, RTYPE_out, not_10_out, FUNC[1], not_12_out);
  or or_15 (out_14, 1'b0, SH);
  or or_16 (out_18, 1'b0, SB);
endmodule

module OPSPLITTER (
  input  [31:0] in_1,
  output [5:0] OP,
  output [4:0] RS,
  output [4:0] RT,
  output [4:0] RD,
  output [4:0] SHAMT,
  output [5:0] FUNC,
  output [15:0] IMME,
  output [25:0] ADDRESS
);


  assign ADDRESS = in_1[25:0];
  assign FUNC = in_1[5:0];
  assign IMME = in_1[15:0];
  assign OP = in_1[31:26];
  assign RD = in_1[15:11];
  assign RS = in_1[25:21];
  assign RT = in_1[20:16];
  assign SHAMT = in_1[10:6];
endmodule

module NPC (
  input  [31:0] in_1,
  input  [31:0] in_2,
  input  in_3,
  input  [25:0] in_4,
  input  in_5,
  input  [31:0] in_6,
  input  in_7,
  output [31:0] out_8
);

  wire comparator_1_eq;
  wire [31:0] adder_1_out, adder_2_out, multiplexer_1_out, multiplexer_2_out, shifter_1_out;

  Comparator #(.width(1), .mode("unsigned")) comparator_1 (.a(in_3), .b(1'b1), .eq(comparator_1_eq));  // open: gt, lt
  Shifter #(.width(32)) shifter_1 (.in(in_2), .\dist (5'b00010), .out(shifter_1_out));
  Adder #(.width(32)) adder_1 (.a(in_1), .b(32'h4), .out(adder_1_out));  // open: cin, cout
  Adder #(.width(32)) adder_2 (.a(adder_1_out), .b(shifter_1_out), .out(adder_2_out));  // open: cin, cout
  Multiplexer #(.width(32)) multiplexer_1 (
    .in0(adder_1_out), .in1(adder_2_out), .out(multiplexer_1_out), .sel(comparator_1_eq));  // open: en
  Multiplexer #(.width(32)) multiplexer_2 (
    .in0(multiplexer_1_out), .in1({in_1[31:28], in_4, 2'b00}), .out(multiplexer_2_out), .sel(in_5));  // open: en
  Multiplexer #(.width(32)) multiplexer_3 (.in0(multiplexer_2_out), .in1(in_6), .out(out_8), .sel(in_7));  // open: en
endmodule

module DM (
  input  [31:0] in_1,
  input  LB,
  input  [31:0] in_3,
  input  MemWrite,
  input  clk,
  input  MemRead,
  input  clr,
  input  SB,
  input  SH,
  input  LH,
  output [4:0] out_11,
  output [31:0] out_12
);

  wire decoder_1_out0, decoder_1_out1, decoder_1_out2, decoder_1_out3, decoder_2_out0, decoder_2_out1;
  wire [7:0] _0, _1, _2, _3, multiplexer_9_out;
  wire [15:0] multiplexer_10_out;
  wire [31:0] bit_extender_1_out, bit_extender_2_out, multiplexer_1_out, multiplexer_2_out,
       multiplexer_3_out, multiplexer_7_out, multiplexer_11_out;

  Multiplexer #(.width(32)) multiplexer_1 (
    .in0(in_3), .in1(multiplexer_3_out), .out(multiplexer_1_out), .sel(SB));  // open: en
  Multiplexer #(.width(32)) multiplexer_2 (
    .in0(multiplexer_1_out), .in1(multiplexer_7_out), .out(multiplexer_2_out), .sel(SH));  // open: en
  Decoder #(.select(2)) decoder_1 (
    .out0(decoder_1_out0), .out1(decoder_1_out1), .out2(decoder_1_out2), .out3(decoder_1_out3),
    .sel(in_1[1:0]));  // open: en
  Decoder decoder_2 (.out0(decoder_2_out0), .out1(decoder_2_out1), .sel(in_1[1]));  // open: en
  RAM #(.addrWidth(5), .dataWidth(32), .bus("separate")) ram_1 (
    .addr(in_1[6:2]), .din(multiplexer_2_out), .data({_3, _2, _1, _0}), .str(MemWrite), .clk(clk),
    .ld(MemRead), .clr(clr));  // open: sel
  Multiplexer #(.width(8)) multiplexer_3 (
    .in0(_0), .in1(in_3[7:0]), .out(multiplexer_3_out[7:0]), .sel(decoder_1_out0));  // open: en
  Multiplexer #(.width(8)) multiplexer_4 (
    .in0(_1), .in1(in_3[7:0]), .out(multiplexer_3_out[15:8]), .sel(decoder_1_out1));  // open: en
  Multiplexer #(.width(8)) multiplexer_5 (
    .in0(_2), .in1(in_3[7:0]), .out(multiplexer_3_out[23:16]), .sel(decoder_1_out2));  // open: en
  Multiplexer #(.width(8)) multiplexer_6 (
    .in0(_3), .in1(in_3[7:0]), .out(multiplexer_3_out[31:24]), .sel(decoder_1_out3));  // open: en
  Multiplexer #(.width(16)) multiplexer_7 (
    .in0({_1, _0}), .in1(in_3[15:0]), .out(multiplexer_7_out[15:0]), .sel(decoder_2_out0));  // open: en
  Multiplexer #(.width(16)) multiplexer_8 (
    .in0({_3, _2}), .in1(in_3[15:0]), .out(multiplexer_7_out[31:16]), .sel(decoder_2_out1));  // open: en
  Multiplexer #(.select(2), .width(8)) multiplexer_9 (
    .in0(_0), .in1(_1), .in2(_2), .in3(_3), .out(multiplexer_9_out), .sel(in_1[1:0]));  // open: en
  Multiplexer #(.width(16)) multiplexer_10 (
    .in0({_1, _0}), .in1({_3, _2}), .out(multiplexer_10_out), .sel(in_1[1]));  // open: en
  assign bit_extender_1_out = {{24{multiplexer_9_out[7]}}, multiplexer_9_out};  // Bit_Extender bit_extender_1
  assign bit_extender_2_out = {{16{multiplexer_10_out[15]}}, multiplexer_10_out};  // Bit_Extender bit_extender_2
  Multiplexer #(.width(32)) multiplexer_11 (
    .in0({_3, _2, _1, _0}), .in1(bit_extender_1_out), .out(multiplexer_11_out), .sel(LB));  // open: en
  Multiplexer #(.width(32)) multiplexer_12 (
    .in0(multiplexer_11_out), .in1(bit_extender_2_out), .out(out_12), .sel(LH));  // open: en

  assign out_11 = in_1[6:2];
endmodule

module EXT (
  input  [15:0] in_1,
  input  [1:0] in_2,
  output [31:0] out_3
);

  wire [31:0] bit_extender_1_out, bit_extender_2_out;

  assign bit_extender_1_out = {{16{1'b0}}, in_1};  // Bit_Extender bit_extender_1
  assign bit_extender_2_out = {{16{in_1[15]}}, in_1};  // Bit_Extender bit_extender_2
  Multiplexer #(.select(2), .width(32)) multiplexer_1 (
    .in0(bit_extender_1_out), .in1(bit_extender_2_out), .in2({in_1, {16{1'b0}}}), .out(out_3), .sel(in_2));  // open: in3, en
endmodule
